# Fritzing sketch MR-990 (saved by Fritzing 1.0.3b)
breadboards: 2

parts:
  DIN1 = DIN-5 jack (MIDI) [package=THT]
  Componente1 = Arduino Mega 2560 (Rev3)
  R1 = Resistor [tolerance=±5% resistance=220 package="0805 [SMD]"]
  microSD1 = MicroSD Card Module
  Teensy2 = Teensy 4.1

nets:
  N1: DIN1.5, Componente1.D18/TX1
  GND: DIN1.2, Componente1.GND, microSD1.GND
  N2: DIN1.4, R1.Pin_0
  5V: Componente1.5V, R1.Pin_1, microSD1.VCC
  N3: Componente1.D50, microSD1.MISO
  N4: Componente1.D51, microSD1.MOSI
  N5: Componente1.D52, microSD1.SCK
  N6: Componente1.D53, microSD1.CS
  N7: Teensy2.GND, Teensy2.GND2#55

custom parts:
  Teensy 4.1: The Teensy is a complete USB-based microcontoller development system, in a very small footprint, capable of implementing many types of projects. All programming is done via the USB port. No special programmer is needed, only a standard micro-USB cable and a PC or Macintosh with a USB port.
